# Fritzing sketch GatePi (saved by Fritzing 0.9.3b)
breadboards: 1

parts:
  Hoftor = M16 [package=1x16_machine-pin-header_lock.004]
  Pi = M16 [package=1x16_machine-pin-header_lock.004]
  U1 = Sharp PC817 [package=THT]
  Q1 = NPN-Transistor [package="TO92 [THT]"]
  R1 = Resistor [tolerance=±5% resistance=47k package=THT]
  R2 = Resistor [tolerance=±5% resistance=1k package=THT]
  R3 = Resistor [tolerance=±5% resistance=1k package=THT]
  U2 = Sharp PC817 [package=THT]
  Q2 = NPN-Transistor [package="TO92 [THT]"]
  R4 = Resistor [tolerance=±5% resistance=4.7k package=THT]
  R5 = Resistor [tolerance=±5% resistance=1k package=THT]
  R6 = Resistor [tolerance=±5% resistance=10k package=THT]
  R7 = Resistor [tolerance=±5% resistance=1k package=THT]
  U3 = Sharp PC817 [package=THT]
  R8 = Resistor [tolerance=±5% resistance=220 package=THT]
  Q3 = NPN-Transistor [package="TO92 [THT]"]
  R9 = Resistor [tolerance=±5% resistance=10k package=THT]
  R10 = Resistor [tolerance=±5% resistance=1k package=THT]
  U4 = Sharp PC817 [package=THT]
  R11 = Resistor [tolerance=±5% resistance=100 package=THT]
  R12 = Resistor [tolerance=±5% resistance=1k package=THT]
  R13 = Resistor [tolerance=±5% resistance=1k package=THT]
  Q4 = NPN-Transistor [package="TO92 [THT]"]
  R14 = Resistor [tolerance=±5% resistance=47k package=THT]
  R15 = Resistor [tolerance=±5% resistance=1k package=THT]
  R16 = Resistor [tolerance=±5% resistance=4.7k package=THT]
  R17 = Resistor [tolerance=±5% resistance=47k package=THT]
  Q5 = NPN-Transistor [package="TO92 [THT]"]

nets:
  N1: Hoftor.1, R3.Pin_1
  N2: Hoftor.2, R6.Pin_1
  N3: Hoftor.3, Hoftor.6, R4.Pin_0, R8.Pin_1
  N4: Hoftor.4, Q5.E
  N5: Hoftor.5, U1.Pin_4, Q2.E, Q3.E, R11.Pin_0, Q5.C
  N6: Hoftor.7, R9.Pin_1, U4.Pin_4
  N7: Hoftor.8, Pi.11
  N8: Hoftor.9, Hoftor.10, Hoftor.13, R15.Pin_0
  N9: Hoftor.11, Pi.12
  N10: Hoftor.12, Pi.13
  N11: Hoftor.14, Pi.4, Pi.14, R2.Pin_1, R5.Pin_1, R12.Pin_1, R13.Pin_1, R16.Pin_1
  N12: Hoftor.15, Pi.3, Pi.15, Q1.E, U2.Pin_3, U3.Pin_3, Q4.E, R15.Pin_1
  N13: Hoftor.16, Pi.16, R16.Pin_0
  N14: Pi.1, R1.Pin_0
  N15: Pi.2, R7.Pin_1
  N16: Pi.7, R10.Pin_0
  N17: Pi.8, R14.Pin_0
  N18: Pi.10, R17.Pin_0
  N19: U1.Pin_1, R2.Pin_0, R5.Pin_0
  N20: U1.Pin_2, Q1.C
  N21: U1.Pin_3, R3.Pin_0
  N22: Q1.B, R1.Pin_1
  N23: U2.Pin_1, R4.Pin_1
  N24: U2.Pin_2, Q2.C
  N25: U2.Pin_4, R7.Pin_0
  N26: Q2.B, R6.Pin_0
  N27: U3.Pin_1, R8.Pin_0
  N28: U3.Pin_2, Q3.C
  N29: U3.Pin_4, R10.Pin_1
  N30: Q3.B, R9.Pin_0
  N31: U4.Pin_1, R12.Pin_0, R13.Pin_0
  N32: U4.Pin_2, Q4.C
  N33: U4.Pin_3, R11.Pin_1
  N34: Q4.B, R14.Pin_1
  N35: R17.Pin_1, Q5.B
